# Fritzing sketch Core (saved by Fritzing 0.9.3b)
breadboards: 1

parts:
  DHT3 = DHT11 Humitidy and Temperature Sensor [part_number=DHT11]
  Part1 = Arduino Uno (Rev3)
  U1 = NodeMCU V2.0
  U4 = 2-Channel 5v Relay Shield [package=relay-2ch5v10a]
  U5 = GAS_SENSOR [package=mq-3]
  Part2 = Soil Moisture Sensor
  U6 = GAS_SENSOR [package=mq-3]

nets:
  VCC: DHT3.VDD, Part1.A0, Part1.5V, U1.Vin, U4.VCC, U5.B1, Part2.VCC, U6.B1
  N1: DHT3.DATA, Part1.D4
  GND: DHT3.GND, Part1.A1, Part1.GND, U1.GND, U4.GND, U5.A1, Part2.GND, U6.A1
  N2: Part1.D2, U1.D2
  N3: Part1.D3_PWM, U1.D3
  N4: U1.D5, U4.IN1
  N5: U1.D6, U4.IN2

notes:
  ต่อกับ Adapter 7V-12V (แนะนำ 9V)
  O2 Sensor - ต่อขา Sig เข้ากับ Arduino Uno ขา A2
  DHT22 - ต่อขา out เข้ากับ Arduino Uno ขา 4
  จ่ายไฟ 5V จาก Arduino Uno สำหรับเซนเซอร์ต่างๆ และ NodeMCU v2
  ต่อ output จาก Relay 1 เพื่อไปเปิด/ปิดวาล์วหรือปั้มนำ (ขึ้นอยู่กับระบบน้ำที่สวนมะนาวใช้งาน)
  Relay 2 สามารถนำไปต่อกับพัดลมหรือสวิตช์ ต่างๆ ที่จะทำการวิจัย ต่อไปได้ในอนาคต
  Soi Moisture and PH sensor ต่อเข้ากับ Arduino Uno ขา A0, A1 ตามลำดับ
  CO2 Sensor -
  ต่อขา 10 (Tx) เข้ากับ Arduino Uno ขา A4
  ต่อขอ 11(Rx) เข้ากับ Arduino ขา A5
  NodeMCU V2 ขา D2,D3 ต่อเข้ากับ Arduino Uno ขา 2,3ตามลำดับ

custom parts:
  DHT11 Humitidy and Temperature Sensor: DHT11 Humidity and Temperature Sensor
  NodeMCU V2.0: ESP8266 based NodeMCU
  2-Channel 5v Relay Shield: 2 Channel 5v Relay Shield w. 2x SPD-06VDC-SD-C
